# Fritzing sketch fan_circuit (saved by Fritzing 0.9.3b)
breadboards: 1

parts:
  Q1 = PNP-Transistor [package="TO92 [THT]"]
  F1 = Fan - Ventilador [package=THT]
  R1 = Resistor [tolerance=±5% resistance=220 package="2512 [SMD]"]
  Raspberry_Pi_3 = Raspberry Pi 3 [part_number=RPI-3-V1.2]

nets (from the schematic view):
  N1: Q1.E, F1.GND
  N2: Q1.B, R1.Pin_0
  N3: Q1.C, Raspberry_Pi_3.GND
  5V: F1.5V, Raspberry_Pi_3.5V
  N4: R1.Pin_1, Raspberry_Pi_3.GPIO14

custom parts:
  Fan - Ventilador: Ventilador de 2 pines, se encuentra comunmente en computadoras de escritorio
